// Logisim project mico_x1.circ as structural Verilog: 9 circuits, main circuit Mico_X1
module Mico_X1 (
  input  in_1
);

  wire and_1_out, BRWE, CLK, CTE, DWE, multiplexer_2_out, zero;
  wire [1:0] JMP, Memoria_de_controle_data;
  wire [2:0] sULA;
  wire [3:0] Memoria_de_programa_demo_data, Memoria_de_programa_demo_data_2, Memoria_de_programa_demo_data_3,
       Memoria_de_programa_demo_data_4, Memoria_de_programa_demo_data_5, Memoria_de_programa_demo_data_6,
       Memoria_de_programa_demo_data_7, Memoria_de_programa_demo_data_8;
  wire [31:0] banco_de_registradores_16x32b_1_outa, banco_de_registradores_16x32b_1_outb, bit_extender_1_out,
       bit_extender_2_out, carrylookahead_adder_32b_1_s, IP_q, multiplexer_1_p4, multiplexer_4_out,
       unidade_logico_aritmetica_1_s;

  assign bit_extender_1_out = {{16{Memoria_de_programa_demo_data_4[3]}}, {Memoria_de_programa_demo_data_4, Memoria_de_programa_demo_data_3, Memoria_de_programa_demo_data_2, Memoria_de_programa_demo_data}};  // Bit_Extender bit_extender_1
  // Multiplexer #(.select(2), .width(32)) multiplexer_1: pin names not known; wires that end beside it: 32'h1, bit_extender_1_out, {32{1'b0}}, multiplexer_1_p4, JMP
  Multiplexer #(.select(2)) multiplexer_2 (
    .in0(1'b0), .in1(bit_extender_1_out[31]), .in2(1'b0), .out(multiplexer_2_out));  // open: in3, sel
  CarryLookAhead_adder_32b carrylookahead_adder_32b_1 (
    .A(IP_q), .B(multiplexer_1_p4), .Cin(multiplexer_2_out), .S(carrylookahead_adder_32b_1_s));
  Register #(.width(32)) IP (.D(carrylookahead_adder_32b_1_s), .en(1'b1), .clk(CLK), .Q(IP_q), .clr(in_1));
  Clock clock_1 (.out(CLK));
  ROM #(.addrWidth(24), .dataWidth(32)) Memoria_de_programa_demo (
    .addr(IP_q[23:0]),
    .data({Memoria_de_programa_demo_data_8, Memoria_de_programa_demo_data_7, Memoria_de_programa_demo_data_6, Memoria_de_programa_demo_data_5, Memoria_de_programa_demo_data_4, Memoria_de_programa_demo_data_3, Memoria_de_programa_demo_data_2, Memoria_de_programa_demo_data}));
  ROM #(.addrWidth(4)) Memoria_de_controle (
    .addr(Memoria_de_programa_demo_data_8), .data({sULA, Memoria_de_controle_data, CTE, BRWE, DWE}));
  Banco_de_Registradores_16x32b banco_de_registradores_16x32b_1 (
    .reset(in_1), .endA(Memoria_de_programa_demo_data_7), .endB(Memoria_de_programa_demo_data_6), .WE(BRWE),
    .endC(Memoria_de_programa_demo_data_5), .dataC(unidade_logico_aritmetica_1_s), .CLK(CLK),
    .outA(banco_de_registradores_16x32b_1_outa), .outB(banco_de_registradores_16x32b_1_outb));
  assign bit_extender_2_out = {{16{1'b0}}, {Memoria_de_programa_demo_data_4, Memoria_de_programa_demo_data_3, Memoria_de_programa_demo_data_2, Memoria_de_programa_demo_data}};  // Bit_Extender bit_extender_2
  and and_1 (and_1_out, sULA[0], zero);
  Multiplexer #(.width(2)) multiplexer_3 (.in0(Memoria_de_controle_data), .in1(2'b01), .out(JMP));  // open: sel
  Register #(.width(32)) display (
    .D(banco_de_registradores_16x32b_1_outa), .en(DWE), .clk(CLK), .clr(in_1));  // open: Q
  Unidade_Logico_Aritmetica unidade_logico_aritmetica_1 (
    .A(banco_de_registradores_16x32b_1_outa), .B(multiplexer_4_out), .seletor(sULA),
    .S(unidade_logico_aritmetica_1_s), .zero(zero));
  Multiplexer #(.width(32)) multiplexer_4 (
    .in0(banco_de_registradores_16x32b_1_outb), .in1(bit_extender_2_out), .out(multiplexer_4_out), .sel(CTE));
  ROM #(.addrWidth(24), .dataWidth(32)) Memoria_de_programa_fib ();  // open: addr, data

  // Other names for the same wires on the sheet: reset = in_1

  // Notes on the sheet:
  //   contents of Memoria_de_programa_demo (hex, n*v repeats v):
  //   0 b001000a e1200004 b2020001 c2000000 d000fffc 30220000 c2000000 b0020005 c2000000 11230000 c3000000
  //   23140000 c4000000 64040000 c4000000 44250000 c5000000 55060000 c6000000 76260000 c6000000 86260000
  //   c6000000 9505ffff c5000000 a505ffff c5000000 f0000000
  //   contents of Memoria_de_controle (hex, n*v repeats v):
  //   0 2 22 42 62 82 a2 c2 e2 66 86 6 1 8 20 10
  //   contents of Memoria_de_programa_fib (hex, n*v repeats v):
  //   b001000a b0030001 b0040001 e1200007 c3000000 13450000 10430000 10540000 b2020001 d000fff9 f0000000
  //   17*0 f0000000
endmodule

// ULA
module Unidade_Logico_Aritmetica (
  input  [31:0] A,
  input  [2:0] seletor,
  input  [31:0] B,
  output zero,
  output [31:0] S
);

  wire [31:0] and_1_out, Lshift_s, not_1_out, not_2_out, or_1_out, Rshift_s, soma_s, subtracao_s, xor_1_out;

  CarryLookAhead_adder_32b soma (.A(A), .B(B), .Cin(1'b0), .S(soma_s));
  CarryLookAhead_adder_32b subtracao (.A(A), .B(not_1_out), .Cin(1'b1), .S(subtracao_s));
  assign not_1_out = ~B;  // NOT_Gate not_1, 32 bits wide
  Left_Shifter_32b Lshift (.B(B), .A(A), .S(Lshift_s));
  Right_Shifter_32b Rshift (.B(B), .A(A), .S(Rshift_s));
  assign and_1_out = A & B;  // AND_Gate and_1, 32 bits wide
  assign or_1_out = A | B;  // OR_Gate or_1, 32 bits wide
  assign xor_1_out = A ^ B;  // XOR_Gate xor_1, 32 bits wide
  assign not_2_out = ~A;  // NOT_Gate not_2, 32 bits wide
  Multiplexer #(.select(3), .width(32)) multiplexer_1 (
    .in0(soma_s), .in1(subtracao_s), .in2(and_1_out), .in3(or_1_out), .in4(xor_1_out), .in5(not_2_out),
    .in6(Lshift_s), .in7(Rshift_s), .out(S), .sel(seletor));
  nor nor_1 (zero, S[0], S[1], S[2], S[3], S[4], S[5], S[6], S[7], S[8], S[9], S[10], S[11], S[12], S[13], S[14], S[15], S[17], S[18], S[19], S[20], S[21], S[22], S[23], S[24], S[25], S[26], S[27], S[28], S[29], S[30], S[31], S[16]);
endmodule

// BancoReg16x32b
module Banco_de_Registradores_16x32b (
  input  [31:0] dataC,
  input  [3:0] endA,
  input  WE,
  input  [3:0] endC,
  input  [3:0] endB,
  input  CLK,
  input  reset,
  output [31:0] outA,
  output [31:0] outB
);

  wire demultiplexer_1_out0, demultiplexer_1_out1, demultiplexer_1_out2, demultiplexer_1_out3,
       demultiplexer_1_out4, demultiplexer_1_out5, demultiplexer_1_out6, demultiplexer_1_out7,
       demultiplexer_1_out8, demultiplexer_1_out9, demultiplexer_1_out10, demultiplexer_1_out11,
       demultiplexer_1_out12, demultiplexer_1_out13, demultiplexer_1_out14, demultiplexer_1_out15;
  wire [31:0] r0, r1, r2, r3, r4, r5, r6, r7, r8, r9, r10, r11, r12, r13, r14, r15;

  Demultiplexer #(.select(4)) demultiplexer_1 (
    .out0(demultiplexer_1_out0), .out1(demultiplexer_1_out1), .out2(demultiplexer_1_out2),
    .out3(demultiplexer_1_out3), .out4(demultiplexer_1_out4), .out5(demultiplexer_1_out5),
    .out6(demultiplexer_1_out6), .out7(demultiplexer_1_out7), .out8(demultiplexer_1_out8),
    .out9(demultiplexer_1_out9), .out10(demultiplexer_1_out10), .out11(demultiplexer_1_out11),
    .out12(demultiplexer_1_out12), .out13(demultiplexer_1_out13), .out14(demultiplexer_1_out14),
    .out15(demultiplexer_1_out15), .in(WE), .sel(endC));
  Register #(.width(32)) register_1 (.D(dataC), .en(demultiplexer_1_out0), .clk(CLK), .Q(r0), .clr(1'b1));
  Register #(.width(32)) register_2 (.D(dataC), .en(demultiplexer_1_out4), .clk(CLK), .Q(r4), .clr(reset));
  Register #(.width(32)) register_3 (.D(dataC), .en(demultiplexer_1_out11), .clk(CLK), .Q(r11), .clr(reset));
  Register #(.width(32)) register_4 (.D(dataC), .en(demultiplexer_1_out15), .clk(CLK), .Q(r15), .clr(reset));
  Register #(.width(32)) register_5 (.D(dataC), .en(demultiplexer_1_out1), .clk(CLK), .Q(r1), .clr(reset));
  Register #(.width(32)) register_6 (.D(dataC), .en(demultiplexer_1_out5), .clk(CLK), .Q(r5), .clr(reset));
  Register #(.width(32)) register_7 (.D(dataC), .en(demultiplexer_1_out10), .clk(CLK), .Q(r10), .clr(reset));
  Register #(.width(32)) register_8 (.D(dataC), .en(demultiplexer_1_out14), .clk(CLK), .Q(r14), .clr(reset));
  Register #(.width(32)) register_9 (.D(dataC), .en(demultiplexer_1_out2), .clk(CLK), .Q(r2), .clr(reset));
  Register #(.width(32)) register_10 (.D(dataC), .en(demultiplexer_1_out6), .clk(CLK), .Q(r6), .clr(reset));
  Register #(.width(32)) register_11 (.D(dataC), .en(demultiplexer_1_out9), .clk(CLK), .Q(r9), .clr(reset));
  Register #(.width(32)) register_12 (.D(dataC), .en(demultiplexer_1_out13), .clk(CLK), .Q(r13), .clr(reset));
  Register #(.width(32)) register_13 (.D(dataC), .en(demultiplexer_1_out3), .clk(CLK), .Q(r3), .clr(reset));
  Register #(.width(32)) register_14 (.D(dataC), .en(demultiplexer_1_out7), .clk(CLK), .Q(r7), .clr(reset));
  Register #(.width(32)) register_15 (.D(dataC), .en(demultiplexer_1_out8), .clk(CLK), .Q(r8), .clr(reset));
  Register #(.width(32)) register_16 (.D(dataC), .en(demultiplexer_1_out12), .clk(CLK), .Q(r12), .clr(reset));
  Multiplexer #(.select(4), .width(32)) multiplexer_1 (
    .in0(r0), .in1(r1), .in2(r2), .in3(r3), .in4(r4), .in5(r5), .in6(r6), .in7(r7), .in8(r8), .in9(r9),
    .in10(r10), .in11(r11), .in12(r12), .in13(r13), .in14(r14), .in15(r15), .out(outA), .sel(endA));
  Multiplexer #(.select(4), .width(32)) multiplexer_2 (
    .in0(r0), .in1(r1), .in2(r2), .in3(r3), .in4(r4), .in5(r5), .in6(r6), .in7(r7), .in8(r8), .in9(r9),
    .in10(r10), .in11(r11), .in12(r12), .in13(r13), .in14(r14), .in15(r15), .out(outB), .sel(endB));
endmodule

// CLAadder32b
module CarryLookAhead_adder_32b (
  input  [31:0] B,
  input  [31:0] A,
  input  Cin,
  output [31:0] S
);

  wire carrylookahead_logic_1_c1, carrylookahead_logic_1_c2, carrylookahead_logic_1_c3,
       carrylookahead_logic_1_gg, carrylookahead_logic_1_pg, carrylookahead_logic_2_c1,
       carrylookahead_logic_3_c1, carrylookahead_logic_3_c2, carrylookahead_logic_3_c3,
       carrylookahead_logic_3_gg, carrylookahead_logic_3_pg, carrylookahead_logic_4b_1_c1,
       carrylookahead_logic_4b_1_c2, carrylookahead_logic_4b_1_c3, carrylookahead_logic_4b_1_gg,
       carrylookahead_logic_4b_1_pg, carrylookahead_logic_4b_2_c1, carrylookahead_logic_4b_2_c2,
       carrylookahead_logic_4b_2_c3, carrylookahead_logic_4b_2_gg, carrylookahead_logic_4b_2_pg,
       carrylookahead_logic_4b_3_c1, carrylookahead_logic_4b_3_c2, carrylookahead_logic_4b_3_c3,
       carrylookahead_logic_4b_3_gg, carrylookahead_logic_4b_3_pg, carrylookahead_logic_4b_4_c1,
       carrylookahead_logic_4b_4_c2, carrylookahead_logic_4b_4_c3, carrylookahead_logic_4b_4_gg,
       carrylookahead_logic_4b_4_pg, carrylookahead_logic_4b_5_c1, carrylookahead_logic_4b_5_c2,
       carrylookahead_logic_4b_5_c3, carrylookahead_logic_4b_5_gg, carrylookahead_logic_4b_5_pg,
       carrylookahead_logic_4b_6_c1, carrylookahead_logic_4b_6_c2, carrylookahead_logic_4b_6_c3,
       carrylookahead_logic_4b_6_gg, carrylookahead_logic_4b_6_pg, carrylookahead_logic_4b_7_c1,
       carrylookahead_logic_4b_7_c2, carrylookahead_logic_4b_7_c3, carrylookahead_logic_4b_7_gg,
       carrylookahead_logic_4b_7_pg, carrylookahead_logic_4b_8_c1, carrylookahead_logic_4b_8_c2,
       carrylookahead_logic_4b_8_c3, carrylookahead_logic_4b_8_gg, carrylookahead_logic_4b_8_pg;

  Full_Adder_sem_carry_out full_adder_sem_carry_out_1 (
    .A(A[31]), .B(B[31]), .Cin(carrylookahead_logic_4b_1_c3), .S(S[31]));
  CarryLookAhead_logic_4b carrylookahead_logic_4b_1 (
    .Cin(carrylookahead_logic_1_c3), .A3(A[31]), .B3(B[31]), .A2(A[30]), .B2(B[30]), .A1(A[29]), .B1(B[29]),
    .A0(A[28]), .B0(B[28]), .GG(carrylookahead_logic_4b_1_gg), .PG(carrylookahead_logic_4b_1_pg),
    .C3(carrylookahead_logic_4b_1_c3), .C2(carrylookahead_logic_4b_1_c2), .C1(carrylookahead_logic_4b_1_c1));
  Full_Adder_sem_carry_out full_adder_sem_carry_out_2 (
    .A(A[30]), .B(B[30]), .Cin(carrylookahead_logic_4b_1_c2), .S(S[30]));
  Full_Adder_sem_carry_out full_adder_sem_carry_out_3 (
    .A(A[29]), .B(B[29]), .Cin(carrylookahead_logic_4b_1_c1), .S(S[29]));
  Full_Adder_sem_carry_out full_adder_sem_carry_out_4 (
    .A(A[28]), .B(B[28]), .Cin(carrylookahead_logic_1_c3), .S(S[28]));
  Full_Adder_sem_carry_out full_adder_sem_carry_out_5 (
    .A(A[27]), .B(B[27]), .Cin(carrylookahead_logic_4b_2_c3), .S(S[27]));
  Full_Adder_sem_carry_out full_adder_sem_carry_out_6 (
    .A(A[26]), .B(B[26]), .Cin(carrylookahead_logic_4b_2_c2), .S(S[26]));
  CarryLookAhead_logic_4b carrylookahead_logic_4b_2 (
    .Cin(carrylookahead_logic_1_c2), .A3(A[27]), .B3(B[27]), .A2(A[26]), .B2(B[26]), .A1(A[25]), .B1(B[25]),
    .A0(A[24]), .B0(B[24]), .GG(carrylookahead_logic_4b_2_gg), .PG(carrylookahead_logic_4b_2_pg),
    .C3(carrylookahead_logic_4b_2_c3), .C2(carrylookahead_logic_4b_2_c2), .C1(carrylookahead_logic_4b_2_c1));
  Full_Adder_sem_carry_out full_adder_sem_carry_out_7 (
    .A(A[25]), .B(B[25]), .Cin(carrylookahead_logic_4b_2_c1), .S(S[25]));
  Full_Adder_sem_carry_out full_adder_sem_carry_out_8 (
    .A(A[24]), .B(B[24]), .Cin(carrylookahead_logic_1_c2), .S(S[24]));
  Full_Adder_sem_carry_out full_adder_sem_carry_out_9 (
    .A(A[23]), .B(B[23]), .Cin(carrylookahead_logic_4b_3_c3), .S(S[23]));
  CarryLookAhead_logic_4b carrylookahead_logic_4b_3 (
    .Cin(carrylookahead_logic_1_c1), .A3(A[23]), .B3(B[23]), .A2(A[22]), .B2(B[22]), .A1(A[21]), .B1(B[21]),
    .A0(A[20]), .B0(B[20]), .GG(carrylookahead_logic_4b_3_gg), .PG(carrylookahead_logic_4b_3_pg),
    .C3(carrylookahead_logic_4b_3_c3), .C2(carrylookahead_logic_4b_3_c2), .C1(carrylookahead_logic_4b_3_c1));
  Full_Adder_sem_carry_out full_adder_sem_carry_out_10 (
    .A(A[22]), .B(B[22]), .Cin(carrylookahead_logic_4b_3_c2), .S(S[22]));
  Full_Adder_sem_carry_out full_adder_sem_carry_out_11 (
    .A(A[21]), .B(B[21]), .Cin(carrylookahead_logic_4b_3_c1), .S(S[21]));
  CarryLookAhead_logic carrylookahead_logic_1 (
    .G3(carrylookahead_logic_4b_1_gg), .P3(carrylookahead_logic_4b_1_pg), .G2(carrylookahead_logic_4b_2_gg),
    .P2(carrylookahead_logic_4b_2_pg), .G1(carrylookahead_logic_4b_3_gg), .P1(carrylookahead_logic_4b_3_pg),
    .G0(carrylookahead_logic_4b_4_gg), .P0(carrylookahead_logic_4b_4_pg), .Cin(carrylookahead_logic_2_c1),
    .GG(carrylookahead_logic_1_gg), .PG(carrylookahead_logic_1_pg), .C3(carrylookahead_logic_1_c3),
    .C2(carrylookahead_logic_1_c2), .C1(carrylookahead_logic_1_c1));
  Full_Adder_sem_carry_out full_adder_sem_carry_out_12 (
    .A(A[20]), .B(B[20]), .Cin(carrylookahead_logic_1_c1), .S(S[20]));
  Full_Adder_sem_carry_out full_adder_sem_carry_out_13 (
    .A(A[19]), .B(B[19]), .Cin(carrylookahead_logic_4b_4_c3), .S(S[19]));
  Full_Adder_sem_carry_out full_adder_sem_carry_out_14 (
    .A(A[18]), .B(B[18]), .Cin(carrylookahead_logic_4b_4_c2), .S(S[18]));
  CarryLookAhead_logic_4b carrylookahead_logic_4b_4 (
    .Cin(carrylookahead_logic_2_c1), .A3(A[19]), .B3(B[19]), .A2(A[18]), .B2(B[18]), .A1(A[17]), .B1(B[17]),
    .A0(A[16]), .B0(B[16]), .GG(carrylookahead_logic_4b_4_gg), .PG(carrylookahead_logic_4b_4_pg),
    .C3(carrylookahead_logic_4b_4_c3), .C2(carrylookahead_logic_4b_4_c2), .C1(carrylookahead_logic_4b_4_c1));
  Full_Adder_sem_carry_out full_adder_sem_carry_out_15 (
    .A(A[17]), .B(B[17]), .Cin(carrylookahead_logic_4b_4_c1), .S(S[17]));
  CarryLookAhead_logic carrylookahead_logic_2 (
    .G1(carrylookahead_logic_1_gg), .P1(carrylookahead_logic_1_pg), .G0(carrylookahead_logic_3_gg),
    .P0(carrylookahead_logic_3_pg), .Cin(Cin), .C1(carrylookahead_logic_2_c1));  // open: G3, P3, G2, P2, GG, PG, C3, C2
  Full_Adder_sem_carry_out full_adder_sem_carry_out_16 (
    .A(A[16]), .B(B[16]), .Cin(carrylookahead_logic_2_c1), .S(S[16]));
  Full_Adder_sem_carry_out full_adder_sem_carry_out_17 (
    .A(A[15]), .B(B[15]), .Cin(carrylookahead_logic_4b_5_c3), .S(S[15]));
  CarryLookAhead_logic_4b carrylookahead_logic_4b_5 (
    .Cin(carrylookahead_logic_3_c3), .A3(A[15]), .B3(B[15]), .A2(A[14]), .B2(B[14]), .A1(A[13]), .B1(B[13]),
    .A0(A[12]), .B0(B[12]), .GG(carrylookahead_logic_4b_5_gg), .PG(carrylookahead_logic_4b_5_pg),
    .C3(carrylookahead_logic_4b_5_c3), .C2(carrylookahead_logic_4b_5_c2), .C1(carrylookahead_logic_4b_5_c1));
  Full_Adder_sem_carry_out full_adder_sem_carry_out_18 (
    .A(A[14]), .B(B[14]), .Cin(carrylookahead_logic_4b_5_c2), .S(S[14]));
  Full_Adder_sem_carry_out full_adder_sem_carry_out_19 (
    .A(A[13]), .B(B[13]), .Cin(carrylookahead_logic_4b_5_c1), .S(S[13]));
  Full_Adder_sem_carry_out full_adder_sem_carry_out_20 (
    .A(A[12]), .B(B[12]), .Cin(carrylookahead_logic_3_c3), .S(S[12]));
  Full_Adder_sem_carry_out full_adder_sem_carry_out_21 (
    .A(A[11]), .B(B[11]), .Cin(carrylookahead_logic_4b_6_c3), .S(S[11]));
  Full_Adder_sem_carry_out full_adder_sem_carry_out_22 (
    .A(A[10]), .B(B[10]), .Cin(carrylookahead_logic_4b_6_c2), .S(S[10]));
  CarryLookAhead_logic_4b carrylookahead_logic_4b_6 (
    .Cin(carrylookahead_logic_3_c2), .A3(A[11]), .B3(B[11]), .A2(A[10]), .B2(B[10]), .A1(A[9]), .B1(B[9]),
    .A0(A[8]), .B0(B[8]), .GG(carrylookahead_logic_4b_6_gg), .PG(carrylookahead_logic_4b_6_pg),
    .C3(carrylookahead_logic_4b_6_c3), .C2(carrylookahead_logic_4b_6_c2), .C1(carrylookahead_logic_4b_6_c1));
  Full_Adder_sem_carry_out full_adder_sem_carry_out_23 (
    .A(A[9]), .B(B[9]), .Cin(carrylookahead_logic_4b_6_c1), .S(S[9]));
  Full_Adder_sem_carry_out full_adder_sem_carry_out_24 (.A(A[8]), .B(B[8]), .Cin(carrylookahead_logic_3_c2), .S(S[8]));
  Full_Adder_sem_carry_out full_adder_sem_carry_out_25 (
    .A(A[7]), .B(B[7]), .Cin(carrylookahead_logic_4b_7_c3), .S(S[7]));
  CarryLookAhead_logic_4b carrylookahead_logic_4b_7 (
    .Cin(carrylookahead_logic_3_c1), .A3(A[7]), .B3(B[7]), .A2(A[6]), .B2(B[6]), .A1(A[5]), .B1(B[5]),
    .A0(A[4]), .B0(B[4]), .GG(carrylookahead_logic_4b_7_gg), .PG(carrylookahead_logic_4b_7_pg),
    .C3(carrylookahead_logic_4b_7_c3), .C2(carrylookahead_logic_4b_7_c2), .C1(carrylookahead_logic_4b_7_c1));
  Full_Adder_sem_carry_out full_adder_sem_carry_out_26 (
    .A(A[6]), .B(B[6]), .Cin(carrylookahead_logic_4b_7_c2), .S(S[6]));
  Full_Adder_sem_carry_out full_adder_sem_carry_out_27 (
    .A(A[5]), .B(B[5]), .Cin(carrylookahead_logic_4b_7_c1), .S(S[5]));
  CarryLookAhead_logic carrylookahead_logic_3 (
    .G3(carrylookahead_logic_4b_5_gg), .P3(carrylookahead_logic_4b_5_pg), .G2(carrylookahead_logic_4b_6_gg),
    .P2(carrylookahead_logic_4b_6_pg), .G1(carrylookahead_logic_4b_7_gg), .P1(carrylookahead_logic_4b_7_pg),
    .G0(carrylookahead_logic_4b_8_gg), .P0(carrylookahead_logic_4b_8_pg), .Cin(Cin),
    .GG(carrylookahead_logic_3_gg), .PG(carrylookahead_logic_3_pg), .C3(carrylookahead_logic_3_c3),
    .C2(carrylookahead_logic_3_c2), .C1(carrylookahead_logic_3_c1));
  Full_Adder_sem_carry_out full_adder_sem_carry_out_28 (.A(A[4]), .B(B[4]), .Cin(carrylookahead_logic_3_c1), .S(S[4]));
  Full_Adder_sem_carry_out full_adder_sem_carry_out_29 (
    .A(A[3]), .B(B[3]), .Cin(carrylookahead_logic_4b_8_c3), .S(S[3]));
  Full_Adder_sem_carry_out full_adder_sem_carry_out_30 (
    .A(A[2]), .B(B[2]), .Cin(carrylookahead_logic_4b_8_c2), .S(S[2]));
  CarryLookAhead_logic_4b carrylookahead_logic_4b_8 (
    .Cin(Cin), .A3(A[3]), .B3(B[3]), .A2(A[2]), .B2(B[2]), .A1(A[1]), .B1(B[1]), .A0(A[0]), .B0(B[0]),
    .GG(carrylookahead_logic_4b_8_gg), .PG(carrylookahead_logic_4b_8_pg), .C3(carrylookahead_logic_4b_8_c3),
    .C2(carrylookahead_logic_4b_8_c2), .C1(carrylookahead_logic_4b_8_c1));
  Full_Adder_sem_carry_out full_adder_sem_carry_out_31 (
    .A(A[1]), .B(B[1]), .Cin(carrylookahead_logic_4b_8_c1), .S(S[1]));
  Full_Adder_sem_carry_out full_adder_sem_carry_out_32 (.A(A[0]), .B(B[0]), .Cin(Cin), .S(S[0]));
endmodule

// Lshifter32b
module Left_Shifter_32b (
  input  [31:0] A,
  input  [31:0] B,
  output [31:0] S
);

  wire or_1_out;
  wire [31:0] multiplexer_1_out, multiplexer_2_out, multiplexer_3_out, multiplexer_4_out, multiplexer_5_out;

  Multiplexer #(.width(32)) multiplexer_1 (.in0(A), .in1({A[15:0], {16{1'b0}}}), .out(multiplexer_1_out), .sel(B[4]));
  Multiplexer #(.width(32)) multiplexer_2 (
    .in0(multiplexer_1_out), .in1({multiplexer_1_out[23:0], {8{1'b0}}}), .out(multiplexer_2_out), .sel(B[3]));
  Multiplexer #(.width(32)) multiplexer_3 (
    .in0(multiplexer_2_out), .in1({multiplexer_2_out[27:0], 4'b0000}), .out(multiplexer_3_out), .sel(B[2]));
  Multiplexer #(.width(32)) multiplexer_4 (
    .in0(multiplexer_3_out), .in1({multiplexer_3_out[29:0], 2'b00}), .out(multiplexer_4_out), .sel(B[1]));
  or or_1 (or_1_out, B[31], B[30], B[29], B[28], B[27], B[26], B[25], B[24], B[23], B[22], B[21], B[20], B[19], B[18], B[17], B[16], B[15], B[14], B[13], B[12], B[11], B[10], B[9], B[8], B[7], B[6], B[5]);
  Multiplexer #(.width(32)) multiplexer_5 (
    .in0(multiplexer_4_out), .in1({multiplexer_4_out[30:0], 1'b0}), .out(multiplexer_5_out), .sel(B[0]));
  Multiplexer #(.width(32)) multiplexer_6 (.in0(multiplexer_5_out), .in1({32{1'b0}}), .out(S), .sel(or_1_out));
endmodule

// Rshifter32b
module Right_Shifter_32b (
  input  [31:0] A,
  input  [31:0] B,
  output [31:0] S
);

  wire or_1_out;
  wire [31:0] multiplexer_1_out, multiplexer_2_out, multiplexer_3_out, multiplexer_4_out, multiplexer_5_out;

  Multiplexer #(.width(32)) multiplexer_1 (.in0(A), .in1({{16{1'b0}}, A[31:16]}), .out(multiplexer_1_out), .sel(B[4]));
  Multiplexer #(.width(32)) multiplexer_2 (
    .in0(multiplexer_1_out), .in1({{8{1'b0}}, multiplexer_1_out[31:8]}), .out(multiplexer_2_out), .sel(B[3]));
  Multiplexer #(.width(32)) multiplexer_3 (
    .in0(multiplexer_2_out), .in1({4'b0000, multiplexer_2_out[31:4]}), .out(multiplexer_3_out), .sel(B[2]));
  Multiplexer #(.width(32)) multiplexer_4 (
    .in0(multiplexer_3_out), .in1({2'b00, multiplexer_3_out[31:2]}), .out(multiplexer_4_out), .sel(B[1]));
  or or_1 (or_1_out, B[31], B[30], B[29], B[28], B[27], B[26], B[25], B[24], B[23], B[22], B[21], B[20], B[19], B[18], B[17], B[16], B[15], B[14], B[13], B[12], B[11], B[10], B[9], B[8], B[7], B[6], B[5]);
  Multiplexer #(.width(32)) multiplexer_5 (
    .in0(multiplexer_4_out), .in1({1'b0, multiplexer_4_out[31:1]}), .out(multiplexer_5_out), .sel(B[0]));
  Multiplexer #(.width(32)) multiplexer_6 (.in0(multiplexer_5_out), .in1({32{1'b0}}), .out(S), .sel(or_1_out));
endmodule

// CLAlogic4b
module CarryLookAhead_logic_4b (
  input  Cin,
  input  A3,
  input  B3,
  input  A2,
  input  B2,
  input  A1,
  input  B1,
  input  A0,
  input  B0,
  output GG,
  output PG,
  output C3,
  output C2,
  output C1
);

  wire and_1_out, and_2_out, and_3_out, and_5_out, and_6_out, and_7_out, and_8_out, and_9_out, and_10_out,
       G0_out, G1_out, G2_out, G3_out, P0_out, P1_out, P2_out, P3_out;

  and G3 (G3_out, A3, B3);
  or or_1 (GG, G3_out, and_1_out, and_2_out, and_3_out);
  xor P3 (P3_out, A3, B3);
  and and_1 (and_1_out, P3_out, G2_out);
  and and_2 (and_2_out, P3_out, P2_out, G1_out);
  and and_3 (and_3_out, P3_out, P2_out, P1_out, G0_out);
  and and_4 (PG, P3_out, P2_out, P1_out, P0_out);
  and G2 (G2_out, A2, B2);
  xor P2 (P2_out, A2, B2);
  or or_2 (C3, G2_out, and_5_out, and_6_out, and_7_out);
  and and_5 (and_5_out, P2_out, G1_out);
  and and_6 (and_6_out, P2_out, P1_out, G0_out);
  and and_7 (and_7_out, P2_out, P1_out, P0_out, Cin);
  and G1 (G1_out, A1, B1);
  xor P1 (P1_out, A1, B1);
  or or_3 (C2, G1_out, and_8_out, and_9_out);
  and and_8 (and_8_out, P1_out, G0_out);
  and and_9 (and_9_out, Cin, P1_out, P0_out);
  and G0 (G0_out, A0, B0);
  or or_4 (C1, G0_out, and_10_out);
  xor P0 (P0_out, A0, B0);
  and and_10 (and_10_out, P0_out, Cin);
endmodule

// CLAlogic
module CarryLookAhead_logic (
  input  Cin,
  input  G3,
  input  P3,
  input  G2,
  input  P2,
  input  G1,
  input  P1,
  input  G0,
  input  P0,
  output C3,
  output C2,
  output C1,
  output GG,
  output PG
);

  wire and_1_out, and_2_out, and_3_out, and_5_out, and_6_out, and_7_out, and_8_out, and_9_out, and_10_out;

  and and_1 (and_1_out, P3, G2);
  or or_1 (GG, G3, and_1_out, and_2_out, and_3_out);
  and and_2 (and_2_out, P3, P2, G1);
  and and_3 (and_3_out, P3, P2, P1, G0);
  and and_4 (PG, P3, P2, P1, P0);
  or or_2 (C3, G2, and_5_out, and_6_out, and_7_out);
  and and_5 (and_5_out, P2, G1);
  and and_6 (and_6_out, P2, P1, G0);
  and and_7 (and_7_out, P2, P1, P0, Cin);
  or or_3 (C2, G1, and_8_out, and_9_out);
  and and_8 (and_8_out, P1, G0);
  and and_9 (and_9_out, Cin, P1, P0);
  and and_10 (and_10_out, P0, Cin);
  or or_4 (C1, G0, and_10_out);
endmodule

// FA
module Full_Adder_sem_carry_out (
  input  A,
  input  B,
  input  Cin,
  output S
);

  wire xor_1_out;

  xor xor_1 (xor_1_out, A, B);
  xor xor_2 (S, xor_1_out, Cin);
endmodule
