// Logisim project testes_adders.circ as structural Verilog: 3 circuits, main circuit main
module FA (
  input  A,
  input  B,
  input  Cin,
  output Cout,
  output S
);

  wire and_1_out, and_2_out, or_2_out, xor_1_out;

  or or_1 (Cout, and_1_out, and_2_out);
  and and_1 (and_1_out, A, B);
  and and_2 (and_2_out, Cin, or_2_out);
  or or_2 (or_2_out, A, B);
  xor xor_1 (xor_1_out, A, B);
  xor xor_2 (S, xor_1_out, Cin);
endmodule

module main (
  input  in_1,
  input  in_2,
  input  in_3,
  input  A,
  input  B,
  output out_6,
  output out_7,
  output out_8,
  output out_9,
  output out_10,
  output out_11,
  output out_12,
  output out_13,
  output out_14,
  output out_15,
  output out_16,
  output out_17,
  output out_18,
  output out_19,
  output out_20,
  output out_21,
  output out_22,
  output out_23,
  output out_24,
  output out_25,
  output out_26,
  output out_27,
  output out_28,
  output out_29,
  output out_30,
  output out_31,
  output out_32,
  output out_33,
  output out_34,
  output out_35,
  output out_36,
  output out_37,
  output out_38,
  output out_39,
  output out_40,
  output out_41,
  output out_42,
  output out_43,
  output out_44,
  output out_45,
  output out_46,
  output out_47,
  output out_48,
  output out_49,
  output out_50,
  output out_51,
  output out_52,
  output out_53,
  output out_54,
  output out_55,
  output out_56,
  output out_57,
  output out_58,
  output out_59,
  output out_60,
  output out_61,
  output out_62,
  output out_63,
  output out_64,
  output out_65,
  output out_66,
  output out_67,
  output out_68,
  output out_69,
  output out_70,
  output out_71,
  output out_72,
  output out_73,
  output out_74,
  output out_75,
  output out_76,
  output out_77,
  output out_78,
  output out_79,
  output out_80,
  output out_81,
  output out_82,
  output out_83,
  output out_84,
  output out_85,
  output out_86,
  output out_87,
  output out_88,
  output out_89,
  output out_90,
  output out_91,
  output out_92,
  output out_93,
  output out_94,
  output out_95,
  output out_96,
  output out_97,
  output out_98,
  output out_99,
  output out_100,
  output out_101,
  output out_102,
  output out_103,
  output out_104
);

  wire clookahead4b_1_c1, clookahead4b_1_c2, clookahead4b_1_c3, clookahead4b_2_c1, clookahead4b_2_c2,
       clookahead4b_2_c3, clookahead4b_2_c4, clookahead4b_3_c1, clookahead4b_3_c2, clookahead4b_3_c3,
       clookahead4b_3_c4, clookahead4b_4_c1, clookahead4b_4_c2, clookahead4b_4_c3, clookahead4b_4_c4,
       clookahead4b_5_c1, clookahead4b_5_c2, clookahead4b_5_c3, clookahead4b_5_c4, clookahead4b_6_c1,
       clookahead4b_6_c2, clookahead4b_6_c3, clookahead4b_6_c4, clookahead4b_7_c1, clookahead4b_7_c2,
       clookahead4b_7_c3, clookahead4b_7_c4, clookahead4b_8_c1, clookahead4b_8_c2, clookahead4b_8_c3,
       clookahead4b_8_c4, fa_2_cout, fa_2_s, fa_3_cout, fa_4_cout, fa_4_s, fa_5_cout, fa_5_s, fa_7_cout,
       fa_8_cout, fa_8_s, fa_10_cout, fa_11_cout, fa_11_s, fa_12_cout, fa_12_s, fa_14_cout, fa_15_cout,
       fa_15_s, fa_16_cout, fa_16_s, fa_18_cout, fa_20_cout, fa_21_cout, fa_21_s, fa_22_cout, fa_22_s,
       fa_24_cout, fa_25_cout, fa_26_cout, fa_26_s, fa_27_cout, fa_27_s, fa_29_cout, fa_30_cout, fa_30_s,
       fa_31_cout, fa_31_s, fa_33_cout, fa_34_cout, fa_34_s, fa_36_cout, fa_37_cout, fa_37_s, fa_39_cout,
       fa_40_cout, fa_40_s, fa_41_cout, fa_41_s, fa_43_cout, fa_44_cout, fa_44_s, fa_46_cout, fa_47_cout,
       fa_47_s, fa_48_cout, fa_48_s, fa_49_cout, fa_50_cout, fa_51_cout, fa_51_s, fa_52_cout, fa_52_s,
       fa_54_cout, fa_55_cout, fa_55_s, fa_57_cout, fa_58_cout, fa_58_s, fa_60_cout, fa_61_cout, fa_61_s,
       fa_62_cout, fa_62_s, fa_64_cout, fa_65_cout, fa_65_s, fa_66_cout, fa_66_s, fa_68_cout, fa_69_cout,
       fa_69_s, fa_70_cout, fa_70_s, fa_72_cout, fa_73_cout, fa_73_s, fa_75_cout, fa_76_cout, fa_77_cout,
       fa_77_s, fa_79_cout, fa_80_cout, fa_80_s, fa_81_cout, fa_81_s, fa_83_cout, fa_84_cout, fa_84_s,
       fa_86_cout, fa_87_cout, fa_87_s, fa_88_cout, fa_88_s, fa_90_cout, fa_91_cout, fa_91_s, fa_92_cout,
       fa_92_s, fa_94_cout, fa_96_cout, fa_97_cout, fa_97_s, fa_98_cout, fa_98_s, fa_100_cout, fa_101_cout,
       fa_101_s, fa_102_cout, fa_102_s, fa_104_cout, fa_104_s, fa_105_cout, fa_105_s, fa_107_cout, fa_107_s,
       fa_108_cout, fa_108_s, fa_110_cout, fa_110_s, fa_111_cout, fa_111_s, fa_113_cout, fa_113_s,
       fa_115_cout, fa_115_s, fa_116_cout, fa_116_s, fa_118_cout, fa_118_s, fa_119_cout, fa_119_s,
       fa_120_cout, fa_120_s, fa_121_cout, fa_122_cout, fa_123_cout, fa_124_cout, multiplexer_6_out,
       multiplexer_11_out, multiplexer_15_out, multiplexer_20_out, multiplexer_26_out, multiplexer_31_out;

  FA fa_1 (.A(A), .B(B), .Cin(fa_3_cout), .Cout(out_6), .S(out_7));
  FA fa_2 (.A(A), .B(B), .Cin(fa_5_cout), .Cout(fa_2_cout), .S(fa_2_s));
  Multiplexer multiplexer_1 (.in0(fa_2_cout), .in1(fa_4_cout), .out(out_39), .sel(multiplexer_6_out));
  FA fa_3 (.A(A), .B(B), .Cin(fa_7_cout), .Cout(fa_3_cout), .S(out_8));
  FA fa_4 (.A(A), .B(B), .Cin(fa_8_cout), .Cout(fa_4_cout), .S(fa_4_s));
  FA fa_5 (.A(A), .B(B), .Cin(fa_12_cout), .Cout(fa_5_cout), .S(fa_5_s));
  Multiplexer multiplexer_2 (.in0(fa_2_s), .in1(fa_4_s), .out(out_40));  // open: sel
  FA fa_6 (.A(B), .B(A), .Cin(clookahead4b_1_c3), .S(out_73));  // open: Cout
  FA fa_7 (.A(A), .B(B), .Cin(fa_10_cout), .Cout(fa_7_cout), .S(out_9));
  FA fa_8 (.A(A), .B(B), .Cin(fa_11_cout), .Cout(fa_8_cout), .S(fa_8_s));
  Multiplexer multiplexer_3 (.in0(fa_5_s), .in1(fa_8_s), .out(out_41));  // open: sel
  CLookahead4B clookahead4b_1 (
    .A3(A), .B3(B), .A2(A), .B2(B), .A1(A), .B1(B), .A0(A), .B0(B), .Cin(clookahead4b_2_c4), .C4(out_72),
    .C3(clookahead4b_1_c3), .C2(clookahead4b_1_c2), .C1(clookahead4b_1_c1));
  FA fa_9 (.A(B), .B(A), .Cin(clookahead4b_1_c2), .S(out_74));  // open: Cout
  FA fa_10 (.A(A), .B(B), .Cin(fa_14_cout), .Cout(fa_10_cout), .S(out_10));
  FA fa_11 (.A(A), .B(B), .Cin(fa_15_cout), .Cout(fa_11_cout), .S(fa_11_s));
  FA fa_12 (.A(A), .B(B), .Cin(fa_16_cout), .Cout(fa_12_cout), .S(fa_12_s));
  Multiplexer multiplexer_4 (.in0(fa_12_s), .in1(fa_11_s), .out(out_42));  // open: sel
  FA fa_13 (.A(B), .B(A), .Cin(clookahead4b_1_c1), .S(out_75));  // open: Cout
  FA fa_14 (.A(A), .B(B), .Cin(fa_18_cout), .Cout(fa_14_cout), .S(out_11));
  FA fa_15 (.A(A), .B(B), .Cin(1'b1), .Cout(fa_15_cout), .S(fa_15_s));
  FA fa_16 (.A(A), .B(B), .Cin(1'b0), .Cout(fa_16_cout), .S(fa_16_s));
  Multiplexer multiplexer_5 (.in0(fa_16_s), .in1(fa_15_s), .out(out_43));  // open: sel
  FA fa_17 (.A(B), .B(A), .Cin(clookahead4b_2_c4), .S(out_76));  // open: Cout
  FA fa_18 (.A(A), .B(B), .Cin(fa_20_cout), .Cout(fa_18_cout), .S(out_12));
  Multiplexer multiplexer_6 (.in0(fa_22_cout), .in1(fa_21_cout), .out(multiplexer_6_out), .sel(multiplexer_11_out));
  FA fa_19 (.A(B), .B(A), .Cin(clookahead4b_2_c3), .S(out_77));  // open: Cout
  FA fa_20 (.A(A), .B(B), .Cin(fa_24_cout), .Cout(fa_20_cout), .S(out_13));
  FA fa_21 (.A(A), .B(B), .Cin(fa_26_cout), .Cout(fa_21_cout), .S(fa_21_s));
  FA fa_22 (.A(A), .B(B), .Cin(fa_27_cout), .Cout(fa_22_cout), .S(fa_22_s));
  Multiplexer multiplexer_7 (.in0(fa_22_s), .in1(fa_21_s), .out(out_44));  // open: sel
  FA fa_23 (.A(B), .B(A), .Cin(clookahead4b_2_c2), .S(out_78));  // open: Cout
  FA fa_24 (.A(A), .B(B), .Cin(fa_25_cout), .Cout(fa_24_cout), .S(out_14));
  FA fa_25 (.A(A), .B(B), .Cin(fa_29_cout), .Cout(fa_25_cout), .S(out_15));
  FA fa_26 (.A(A), .B(B), .Cin(fa_30_cout), .Cout(fa_26_cout), .S(fa_26_s));
  FA fa_27 (.A(A), .B(B), .Cin(fa_31_cout), .Cout(fa_27_cout), .S(fa_27_s));
  Multiplexer multiplexer_8 (.in0(fa_27_s), .in1(fa_26_s), .out(out_45));  // open: sel
  CLookahead4B clookahead4b_2 (
    .A3(A), .B3(B), .A2(A), .B2(B), .A1(A), .B1(B), .A0(A), .B0(B), .Cin(clookahead4b_3_c4),
    .C4(clookahead4b_2_c4), .C3(clookahead4b_2_c3), .C2(clookahead4b_2_c2), .C1(clookahead4b_2_c1));
  FA fa_28 (.A(B), .B(A), .Cin(clookahead4b_2_c1), .S(out_79));  // open: Cout
  FA fa_29 (.A(A), .B(B), .Cin(fa_33_cout), .Cout(fa_29_cout), .S(out_16));
  FA fa_30 (.A(A), .B(B), .Cin(fa_37_cout), .Cout(fa_30_cout), .S(fa_30_s));
  FA fa_31 (.A(A), .B(B), .Cin(fa_34_cout), .Cout(fa_31_cout), .S(fa_31_s));
  Multiplexer multiplexer_9 (.in0(fa_31_s), .in1(fa_30_s), .out(out_46));  // open: sel
  FA fa_32 (.A(B), .B(A), .Cin(clookahead4b_3_c4), .S(out_80));  // open: Cout
  FA fa_33 (.A(A), .B(B), .Cin(fa_36_cout), .Cout(fa_33_cout), .S(out_17));
  FA fa_34 (.A(A), .B(B), .Cin(1'b0), .Cout(fa_34_cout), .S(fa_34_s));
  Multiplexer multiplexer_10 (.in0(fa_34_s), .in1(fa_37_s), .out(out_47));  // open: sel
  FA fa_35 (.A(B), .B(A), .Cin(clookahead4b_3_c3), .S(out_81));  // open: Cout
  FA fa_36 (.A(A), .B(B), .Cin(fa_39_cout), .Cout(fa_36_cout), .S(out_18));
  FA fa_37 (.A(A), .B(B), .Cin(1'b1), .Cout(fa_37_cout), .S(fa_37_s));
  Multiplexer multiplexer_11 (.in0(fa_41_cout), .in1(fa_40_cout), .out(multiplexer_11_out), .sel(multiplexer_15_out));
  FA fa_38 (.A(B), .B(A), .Cin(clookahead4b_3_c2), .S(out_82));  // open: Cout
  FA fa_39 (.A(A), .B(B), .Cin(fa_43_cout), .Cout(fa_39_cout), .S(out_19));
  FA fa_40 (.A(A), .B(B), .Cin(fa_47_cout), .Cout(fa_40_cout), .S(fa_40_s));
  FA fa_41 (.A(A), .B(B), .Cin(fa_44_cout), .Cout(fa_41_cout), .S(fa_41_s));
  Multiplexer multiplexer_12 (.in0(fa_41_s), .in1(fa_40_s), .out(out_48));  // open: sel
  CLookahead4B clookahead4b_3 (
    .A3(A), .B3(B), .A2(A), .B2(B), .A1(A), .B1(B), .A0(A), .B0(B), .Cin(clookahead4b_4_c4),
    .C4(clookahead4b_3_c4), .C3(clookahead4b_3_c3), .C2(clookahead4b_3_c2), .C1(clookahead4b_3_c1));
  FA fa_42 (.A(B), .B(A), .Cin(clookahead4b_3_c1), .S(out_83));  // open: Cout
  FA fa_43 (.A(A), .B(B), .Cin(fa_46_cout), .Cout(fa_43_cout), .S(out_20));
  FA fa_44 (.A(A), .B(B), .Cin(fa_48_cout), .Cout(fa_44_cout), .S(fa_44_s));
  Multiplexer multiplexer_13 (.in0(fa_44_s), .in1(fa_47_s), .out(out_49));  // open: sel
  FA fa_45 (.A(B), .B(A), .Cin(clookahead4b_4_c4), .S(out_84));  // open: Cout
  FA fa_46 (.A(A), .B(B), .Cin(fa_49_cout), .Cout(fa_46_cout), .S(out_21));
  FA fa_47 (.A(A), .B(B), .Cin(fa_51_cout), .Cout(fa_47_cout), .S(fa_47_s));
  FA fa_48 (.A(A), .B(B), .Cin(fa_52_cout), .Cout(fa_48_cout), .S(fa_48_s));
  FA fa_49 (.A(A), .B(B), .Cin(fa_50_cout), .Cout(fa_49_cout), .S(out_22));
  FA fa_50 (.A(A), .B(B), .Cin(fa_54_cout), .Cout(fa_50_cout), .S(out_23));
  FA fa_51 (.A(A), .B(B), .Cin(fa_55_cout), .Cout(fa_51_cout), .S(fa_51_s));
  FA fa_52 (.A(A), .B(B), .Cin(1'b0), .Cout(fa_52_cout), .S(fa_52_s));
  Multiplexer multiplexer_14 (.in0(fa_48_s), .in1(fa_51_s), .out(out_50));  // open: sel
  FA fa_53 (.A(B), .B(A), .Cin(clookahead4b_4_c3), .S(out_85));  // open: Cout
  FA fa_54 (.A(A), .B(B), .Cin(fa_57_cout), .Cout(fa_54_cout), .S(out_24));
  FA fa_55 (.A(A), .B(B), .Cin(1'b1), .Cout(fa_55_cout), .S(fa_55_s));
  Multiplexer multiplexer_15 (.in0(fa_58_cout), .in1(fa_61_cout), .out(multiplexer_15_out), .sel(multiplexer_20_out));
  Multiplexer multiplexer_16 (.in0(fa_52_s), .in1(fa_55_s), .out(out_51));  // open: sel
  CLookahead4B clookahead4b_4 (
    .A3(A), .B3(B), .A2(A), .B2(B), .A1(A), .B1(B), .A0(A), .B0(B), .Cin(clookahead4b_5_c4),
    .C4(clookahead4b_4_c4), .C3(clookahead4b_4_c3), .C2(clookahead4b_4_c2), .C1(clookahead4b_4_c1));
  FA fa_56 (.A(B), .B(A), .Cin(clookahead4b_4_c2), .S(out_86));  // open: Cout
  FA fa_57 (.A(A), .B(B), .Cin(fa_60_cout), .Cout(fa_57_cout), .S(out_25));
  FA fa_58 (.A(A), .B(B), .Cin(fa_62_cout), .Cout(fa_58_cout), .S(fa_58_s));
  FA fa_59 (.A(B), .B(A), .Cin(clookahead4b_4_c1), .S(out_87));  // open: Cout
  FA fa_60 (.A(A), .B(B), .Cin(fa_64_cout), .Cout(fa_60_cout), .S(out_26));
  FA fa_61 (.A(A), .B(B), .Cin(fa_65_cout), .Cout(fa_61_cout), .S(fa_61_s));
  FA fa_62 (.A(A), .B(B), .Cin(fa_66_cout), .Cout(fa_62_cout), .S(fa_62_s));
  Multiplexer multiplexer_17 (.in0(fa_58_s), .in1(fa_61_s), .out(out_52));  // open: sel
  FA fa_63 (.A(B), .B(A), .Cin(clookahead4b_5_c4), .S(out_88));  // open: Cout
  FA fa_64 (.A(A), .B(B), .Cin(fa_68_cout), .Cout(fa_64_cout), .S(out_27));
  FA fa_65 (.A(A), .B(B), .Cin(fa_69_cout), .Cout(fa_65_cout), .S(fa_65_s));
  FA fa_66 (.A(A), .B(B), .Cin(fa_70_cout), .Cout(fa_66_cout), .S(fa_66_s));
  Multiplexer multiplexer_18 (.in0(fa_62_s), .in1(fa_65_s), .out(out_53));  // open: sel
  FA fa_67 (.A(B), .B(A), .Cin(clookahead4b_5_c3), .S(out_89));  // open: Cout
  FA fa_68 (.A(A), .B(B), .Cin(fa_72_cout), .Cout(fa_68_cout), .S(out_28));
  FA fa_69 (.A(A), .B(B), .Cin(fa_73_cout), .Cout(fa_69_cout), .S(fa_69_s));
  FA fa_70 (.A(A), .B(B), .Cin(1'b0), .Cout(fa_70_cout), .S(fa_70_s));
  Multiplexer multiplexer_19 (.in0(fa_66_s), .in1(fa_69_s), .out(out_54));  // open: sel
  CLookahead4B clookahead4b_5 (
    .A3(A), .B3(B), .A2(A), .B2(B), .A1(A), .B1(B), .A0(A), .B0(B), .Cin(clookahead4b_6_c4),
    .C4(clookahead4b_5_c4), .C3(clookahead4b_5_c3), .C2(clookahead4b_5_c2), .C1(clookahead4b_5_c1));
  FA fa_71 (.A(B), .B(A), .Cin(clookahead4b_5_c2), .S(out_90));  // open: Cout
  FA fa_72 (.A(A), .B(B), .Cin(fa_75_cout), .Cout(fa_72_cout), .S(out_29));
  FA fa_73 (.A(A), .B(B), .Cin(1'b1), .Cout(fa_73_cout), .S(fa_73_s));
  Multiplexer multiplexer_20 (.in0(fa_77_cout), .in1(fa_80_cout), .out(multiplexer_20_out), .sel(multiplexer_26_out));
  Multiplexer multiplexer_21 (.in0(fa_70_s), .in1(fa_73_s), .out(out_55));  // open: sel
  FA fa_74 (.A(B), .B(A), .Cin(clookahead4b_5_c1), .S(out_91));  // open: Cout
  FA fa_75 (.A(A), .B(B), .Cin(fa_76_cout), .Cout(fa_75_cout), .S(out_30));
  FA fa_76 (.A(A), .B(B), .Cin(fa_79_cout), .Cout(fa_76_cout), .S(out_31));
  FA fa_77 (.A(A), .B(B), .Cin(fa_81_cout), .Cout(fa_77_cout), .S(fa_77_s));
  FA fa_78 (.A(B), .B(A), .Cin(clookahead4b_6_c4), .S(out_92));  // open: Cout
  FA fa_79 (.A(A), .B(B), .Cin(fa_83_cout), .Cout(fa_79_cout), .S(out_32));
  FA fa_80 (.A(A), .B(B), .Cin(fa_84_cout), .Cout(fa_80_cout), .S(fa_80_s));
  FA fa_81 (.A(A), .B(B), .Cin(fa_88_cout), .Cout(fa_81_cout), .S(fa_81_s));
  Multiplexer multiplexer_22 (.in0(fa_77_s), .in1(fa_80_s), .out(out_56));  // open: sel
  FA fa_82 (.A(B), .B(A), .Cin(clookahead4b_6_c3), .S(out_93));  // open: Cout
  FA fa_83 (.A(A), .B(B), .Cin(fa_86_cout), .Cout(fa_83_cout), .S(out_33));
  FA fa_84 (.A(A), .B(B), .Cin(fa_87_cout), .Cout(fa_84_cout), .S(fa_84_s));
  Multiplexer multiplexer_23 (.in0(fa_81_s), .in1(fa_84_s), .out(out_57));  // open: sel
  FA fa_85 (.A(B), .B(A), .Cin(clookahead4b_6_c2), .S(out_94));  // open: Cout
  FA fa_86 (.A(A), .B(B), .Cin(fa_90_cout), .Cout(fa_86_cout), .S(out_34));
  FA fa_87 (.A(A), .B(B), .Cin(fa_91_cout), .Cout(fa_87_cout), .S(fa_87_s));
  FA fa_88 (.A(A), .B(B), .Cin(fa_92_cout), .Cout(fa_88_cout), .S(fa_88_s));
  Multiplexer multiplexer_24 (.in0(fa_88_s), .in1(fa_87_s), .out(out_58));  // open: sel
  CLookahead4B clookahead4b_6 (
    .A3(A), .B3(B), .A2(A), .B2(B), .A1(A), .B1(B), .A0(A), .B0(B), .Cin(clookahead4b_7_c4),
    .C4(clookahead4b_6_c4), .C3(clookahead4b_6_c3), .C2(clookahead4b_6_c2), .C1(clookahead4b_6_c1));
  FA fa_89 (.A(B), .B(A), .Cin(clookahead4b_6_c1), .S(out_95));  // open: Cout
  FA fa_90 (.A(A), .B(B), .Cin(fa_94_cout), .Cout(fa_90_cout), .S(out_35));
  FA fa_91 (.A(A), .B(B), .Cin(1'b1), .Cout(fa_91_cout), .S(fa_91_s));
  FA fa_92 (.A(A), .B(B), .Cin(1'b0), .Cout(fa_92_cout), .S(fa_92_s));
  Multiplexer multiplexer_25 (.in0(fa_92_s), .in1(fa_91_s), .out(out_59));  // open: sel
  FA fa_93 (.A(B), .B(A), .Cin(clookahead4b_7_c4), .S(out_96));  // open: Cout
  FA fa_94 (.A(A), .B(B), .Cin(fa_96_cout), .Cout(fa_94_cout), .S(out_36));
  Multiplexer multiplexer_26 (.in0(fa_98_cout), .in1(fa_97_cout), .out(multiplexer_26_out), .sel(multiplexer_31_out));
  FA fa_95 (.A(B), .B(A), .Cin(clookahead4b_7_c3), .S(out_97));  // open: Cout
  FA fa_96 (.A(A), .B(B), .Cin(fa_100_cout), .Cout(fa_96_cout), .S(out_37));
  FA fa_97 (.A(A), .B(B), .Cin(fa_101_cout), .Cout(fa_97_cout), .S(fa_97_s));
  FA fa_98 (.A(A), .B(B), .Cin(fa_102_cout), .Cout(fa_98_cout), .S(fa_98_s));
  Multiplexer multiplexer_27 (.in0(fa_98_s), .in1(fa_97_s), .out(out_60));  // open: sel
  FA fa_99 (.A(B), .B(A), .Cin(clookahead4b_7_c2), .S(out_98));  // open: Cout
  FA fa_100 (.A(A), .B(B), .Cin(in_1), .Cout(fa_100_cout), .S(out_38));
  FA fa_101 (.A(A), .B(B), .Cin(fa_104_cout), .Cout(fa_101_cout), .S(fa_101_s));
  FA fa_102 (.A(A), .B(B), .Cin(fa_105_cout), .Cout(fa_102_cout), .S(fa_102_s));
  Multiplexer multiplexer_28 (.in0(fa_102_s), .in1(fa_101_s), .out(out_61));  // open: sel
  CLookahead4B clookahead4b_7 (
    .A3(A), .B3(B), .A2(A), .B2(B), .A1(A), .B1(B), .A0(A), .B0(B), .Cin(clookahead4b_8_c4),
    .C4(clookahead4b_7_c4), .C3(clookahead4b_7_c3), .C2(clookahead4b_7_c2), .C1(clookahead4b_7_c1));
  FA fa_103 (.A(B), .B(A), .Cin(clookahead4b_7_c1), .S(out_99));  // open: Cout
  FA fa_104 (.A(A), .B(B), .Cin(fa_108_cout), .Cout(fa_104_cout), .S(fa_104_s));
  FA fa_105 (.A(A), .B(B), .Cin(fa_107_cout), .Cout(fa_105_cout), .S(fa_105_s));
  Multiplexer multiplexer_29 (.in0(fa_105_s), .in1(fa_104_s), .out(out_62));  // open: sel
  FA fa_106 (.A(B), .B(A), .Cin(clookahead4b_8_c4), .S(out_100));  // open: Cout
  FA fa_107 (.A(A), .B(B), .Cin(1'b0), .Cout(fa_107_cout), .S(fa_107_s));
  Multiplexer multiplexer_30 (.in0(fa_107_s), .in1(fa_108_s), .out(out_63));  // open: sel
  FA fa_108 (.A(A), .B(B), .Cin(1'b1), .Cout(fa_108_cout), .S(fa_108_s));
  Multiplexer multiplexer_31 (.in0(fa_111_cout), .in1(fa_110_cout), .out(multiplexer_31_out), .sel(fa_121_cout));
  FA fa_109 (.A(B), .B(A), .Cin(clookahead4b_8_c3), .S(out_101));  // open: Cout
  FA fa_110 (.A(A), .B(B), .Cin(fa_115_cout), .Cout(fa_110_cout), .S(fa_110_s));
  FA fa_111 (.A(A), .B(B), .Cin(fa_113_cout), .Cout(fa_111_cout), .S(fa_111_s));
  Multiplexer multiplexer_32 (.in0(fa_111_s), .in1(fa_110_s), .out(out_64));  // open: sel
  CLookahead4B clookahead4b_8 (
    .A3(A), .B3(B), .A2(A), .B2(B), .A1(A), .B1(B), .A0(A), .B0(B), .Cin(in_3), .C4(clookahead4b_8_c4),
    .C3(clookahead4b_8_c3), .C2(clookahead4b_8_c2), .C1(clookahead4b_8_c1));
  FA fa_112 (.A(B), .B(A), .Cin(clookahead4b_8_c2), .S(out_102));  // open: Cout
  FA fa_113 (.A(A), .B(B), .Cin(fa_116_cout), .Cout(fa_113_cout), .S(fa_113_s));
  Multiplexer multiplexer_33 (.in0(fa_113_s), .in1(fa_115_s), .out(out_65));  // open: sel
  FA fa_114 (.A(B), .B(A), .Cin(clookahead4b_8_c1), .S(out_103));  // open: Cout
  FA fa_115 (.A(A), .B(B), .Cin(fa_118_cout), .Cout(fa_115_cout), .S(fa_115_s));
  FA fa_116 (.A(A), .B(B), .Cin(fa_119_cout), .Cout(fa_116_cout), .S(fa_116_s));
  FA fa_117 (.A(B), .B(A), .Cin(in_3), .S(out_104));  // open: Cout
  FA fa_118 (.A(A), .B(B), .Cin(fa_120_cout), .Cout(fa_118_cout), .S(fa_118_s));
  FA fa_119 (.A(A), .B(B), .Cin(1'b0), .Cout(fa_119_cout), .S(fa_119_s));
  Multiplexer multiplexer_34 (.in0(fa_116_s), .in1(fa_118_s), .out(out_66));  // open: sel
  FA fa_120 (.A(A), .B(B), .Cin(1'b1), .Cout(fa_120_cout), .S(fa_120_s));
  Multiplexer multiplexer_35 (.in0(fa_119_s), .in1(fa_120_s), .out(out_67));  // open: sel
  FA fa_121 (.A(A), .B(B), .Cin(fa_122_cout), .Cout(fa_121_cout), .S(out_68));
  FA fa_122 (.A(A), .B(B), .Cin(fa_123_cout), .Cout(fa_122_cout), .S(out_69));
  FA fa_123 (.A(A), .B(B), .Cin(fa_124_cout), .Cout(fa_123_cout), .S(out_70));
  FA fa_124 (.A(A), .B(B), .Cin(in_2), .Cout(fa_124_cout), .S(out_71));
endmodule

module CLookahead4B (
  input  Cin,
  input  A2,
  input  B2,
  input  A1,
  input  B1,
  input  A0,
  input  B0,
  input  A3,
  input  B3,
  output C4,
  output C3,
  output C2,
  output C1
);

  wire and_1_out, and_2_out, and_3_out, and_4_out, and_5_out, and_6_out, and_7_out, and_8_out, and_9_out,
       and_10_out, G0_out, G1_out, G2_out, G3_out, P0_out, P1_out, P2_out, P3_out;

  and G3 (G3_out, A3, B3);
  xor P3 (P3_out, A3, B3);
  and and_1 (and_1_out, P3_out, G2_out);
  or or_1 (C4, G3_out, and_1_out, and_2_out, and_3_out, and_4_out);
  and and_2 (and_2_out, P3_out, P2_out, G1_out);
  and and_3 (and_3_out, P3_out, P2_out, P1_out, G0_out);
  and and_4 (and_4_out, P3_out, P2_out, P1_out, P0_out, Cin);
  and G2 (G2_out, A2, B2);
  or or_2 (C3, G2_out, and_5_out, and_6_out, and_7_out);
  xor P2 (P2_out, A2, B2);
  and and_5 (and_5_out, P2_out, G1_out);
  and and_6 (and_6_out, P2_out, P1_out, G0_out);
  and and_7 (and_7_out, P2_out, P1_out, P0_out, Cin);
  and G1 (G1_out, A1, B1);
  or or_3 (C2, G1_out, and_8_out, and_9_out);
  xor P1 (P1_out, A1, B1);
  and and_8 (and_8_out, P1_out, G0_out);
  and G0 (G0_out, A0, B0);
  and and_9 (and_9_out, Cin, P1_out, P0_out);
  xor P0 (P0_out, A0, B0);
  and and_10 (and_10_out, P0_out, Cin);
  or or_4 (C1, G0_out, and_10_out);
endmodule
